// Logisim project finalresult.circ as structural Verilog: 17 circuits, main circuit main
module main (
  input  in_1,
  input  in_2,
  input  in_3,
  input  in_4,
  output out_5
);

  wire and_1_out, and_2_out, arithmetic_1_out_7, clock_1_out, cu_all_1_branchbeq, cu_all_1_branchbne,
       cu_all_1_immchoose1, cu_all_1_immchoose2, cu_all_1_jump, cu_all_1_memtoreg, cu_all_1_memwrite,
       cu_all_1_regdst, cu_all_1_regwrite, not_1_out, not_2_out, or_1_out;
  wire [2:0] id_1_op, multiplexer_3_out;
  wire [3:0] cu_all_1_out_12, id_1_funct, id_1_rd, id_1_rs, multiplexer_1_out;
  wire [4:0] id_1_out_5, id_1_rt;
  wire [7:0] arithmetic_1_out_6, bit_extender_1_out, id_1_out_8, multiplexer_2_out, multiplexer_4_out,
       n16register_1_out_8, n16register_1_out_9, ram_1_data;
  wire [7:3] multiplexer_3_out_2;
  wire [16:0] id_1_out_9, pc_1_out_8;
  wire [19:0] rom_1_data;

  PC pc_1 (
    .out_8(pc_1_out_8), .in_4(cu_all_1_jump), .in_6(clock_1_out), .in_7(in_2), .in_2(id_1_out_9),
    .in_5(id_1_out_8), .in_1(or_1_out), .in_3(in_4));
  ROM #(.addrWidth(17), .dataWidth(20)) rom_1 (.addr(pc_1_out_8), .data(rom_1_data));  // open: sel
  Clock clock_1 (.out(clock_1_out));
  or or_1 (or_1_out, and_1_out, and_2_out);
  ID id_1 (
    .in_1(rom_1_data), .OP(id_1_op), .RS(id_1_rs), .RT(id_1_rt), .out_5(id_1_out_5), .RD(id_1_rd),
    .FUNCT(id_1_funct), .out_8(id_1_out_8), .out_9(id_1_out_9));
  Multiplexer #(.width(4)) multiplexer_1 (
    .in0(id_1_rt[3:0]), .in1(id_1_rd), .out(multiplexer_1_out), .sel(cu_all_1_regdst));  // open: en
  and and_1 (and_1_out, cu_all_1_branchbeq, arithmetic_1_out_7);
  and and_2 (and_2_out, not_1_out, cu_all_1_branchbne);
  _16Register u_16register_1 (
    .in_1(multiplexer_4_out), .in_2(in_1), .in_4(id_1_rs), .in_5(id_1_rt[3:0]), .in_6(cu_all_1_regwrite),
    .in_7(multiplexer_1_out), .out_8(n16register_1_out_8), .out_9(n16register_1_out_9), .in_3(clock_1_out));
  assign bit_extender_1_out = {{3{1'b0}}, id_1_out_5};  // Bit_Extender bit_extender_1
  CU_all cu_all_1 (
    .in_1(id_1_op), .regdst(cu_all_1_regdst), .memtoreg(cu_all_1_memtoreg), .regwrite(cu_all_1_regwrite),
    .memwrite(cu_all_1_memwrite), .JUMP(cu_all_1_jump), .immchoose1(cu_all_1_immchoose1),
    .immchoose2(cu_all_1_immchoose2), .in_2(id_1_funct), .out_12(cu_all_1_out_12),
    .BRANCHBEQ(cu_all_1_branchbeq), .BRANCHBNE(cu_all_1_branchbne));
  not not_1 (not_1_out, arithmetic_1_out_7);
  Multiplexer #(.width(8)) multiplexer_2 (
    .in0(n16register_1_out_9), .in1(bit_extender_1_out), .out(multiplexer_2_out), .sel(cu_all_1_immchoose1));  // open: en
  Multiplexer #(.width(8)) multiplexer_3 (
    .in0(multiplexer_2_out), .in1(id_1_out_8), .out({multiplexer_3_out_2, multiplexer_3_out}),
    .sel(cu_all_1_immchoose2));  // open: en
  Arithmetic arithmetic_1 (
    .in_1(n16register_1_out_8), .in_2({multiplexer_3_out_2, multiplexer_3_out}), .in_3(multiplexer_3_out),
    .in_4(cu_all_1_out_12), .out_6(arithmetic_1_out_6), .out_7(arithmetic_1_out_7), .out_5(out_5));
  not not_2 (not_2_out, cu_all_1_memtoreg);
  RAM #(.bus("separate")) ram_1 (
    .addr(arithmetic_1_out_6), .din(n16register_1_out_9), .data(ram_1_data), .str(cu_all_1_memwrite),
    .clk(clock_1_out), .ld(not_2_out), .clr(in_3));  // open: sel
  Multiplexer #(.width(8)) multiplexer_4 (
    .in0(ram_1_data), .in1(arithmetic_1_out_6), .out(multiplexer_4_out), .sel(cu_all_1_memtoreg));  // open: en

  // Notes on the sheet:
  //   contents of rom_1 (hex, n*v repeats v):
  //   22240 28159 8565 6a601 42802 e0007 0 92a02 0 0 ac602 a6b0 0 a1b0
endmodule

module FA (
  input  a,
  input  b,
  input  c,
  output out_4,
  output out_5
);

  wire and_1_out, and_2_out, xor_1_out;

  and and_1 (and_1_out, a, b);
  xor xor_1 (xor_1_out, a, b);
  xor xor_2 (out_4, xor_1_out, c);
  and and_2 (and_2_out, xor_1_out, c);
  or or_1 (out_5, and_1_out, and_2_out);
endmodule

module ADC (
  input  Ci,
  input  [7:0] in_2,
  input  [7:0] in_3,
  output [7:0] out_4,
  output Co
);

  wire fa_1_out_5, fa_2_out_5, fa_3_out_5, fa_4_out_5, fa_5_out_5, fa_6_out_5, fa_7_out_5;

  FA fa_1 (.a(in_2[0]), .b(in_3[0]), .c(Ci), .out_4(out_4[0]), .out_5(fa_1_out_5));
  FA fa_2 (.a(in_2[1]), .b(in_3[1]), .c(fa_1_out_5), .out_4(out_4[1]), .out_5(fa_2_out_5));
  FA fa_3 (.a(in_2[2]), .b(in_3[2]), .c(fa_2_out_5), .out_4(out_4[2]), .out_5(fa_3_out_5));
  FA fa_4 (.a(in_2[3]), .b(in_3[3]), .c(fa_3_out_5), .out_4(out_4[3]), .out_5(fa_4_out_5));
  FA fa_5 (.a(in_2[4]), .b(in_3[4]), .c(fa_4_out_5), .out_4(out_4[4]), .out_5(fa_5_out_5));
  FA fa_6 (.a(in_2[5]), .b(in_3[5]), .c(fa_5_out_5), .out_4(out_4[5]), .out_5(fa_6_out_5));
  FA fa_7 (.a(in_2[6]), .b(in_3[6]), .c(fa_6_out_5), .out_4(out_4[6]), .out_5(fa_7_out_5));
  FA fa_8 (.a(in_2[7]), .b(in_3[7]), .c(fa_7_out_5), .out_4(out_4[7]), .out_5(Co));

  // Notes on the sheet:
  //   A
  //   B
  //   S
endmodule

module Arithmetic (
  input  [7:0] in_1,
  input  [7:0] in_2,
  input  [2:0] in_3,
  input  [3:0] in_4,
  output out_5,
  output [7:0] out_6,
  output out_7
);

  wire [7:0] artic_1_out_5, logic_1_out_4, move_1_out_4;

  move move_1 (.in_1(in_1), .in_2(in_3), .in_3(in_4[1:0]), .out_4(move_1_out_4));
  artic artic_1 (.in_2(in_2), .in_3(in_4[1:0]), .out_5(artic_1_out_5), .in_1(in_1), .out_4(out_5));
  \logic  logic_1 (.in_1(in_1), .in_2(in_2), .in_3(in_4[1:0]), .out_4(logic_1_out_4));
  Multiplexer #(.select(2), .width(8)) multiplexer_1 (
    .in0(artic_1_out_5), .in1(logic_1_out_4), .in2(move_1_out_4), .out(out_6), .sel(in_4[3:2]));  // open: in3, en
  nor nor_1 (out_7, out_6[0], out_6[1], out_6[2], out_6[3], out_6[4], out_6[5], out_6[6], out_6[7]);
endmodule

module substractor (
  input  [7:0] A,
  input  SUB,
  input  [7:0] in_3,
  output [7:0] out_4,
  output Co
);

  wire [7:0] xor_1_out;

  xor xor_1 (xor_1_out[0], in_3[0], SUB);
  xor xor_2 (xor_1_out[1], in_3[1], SUB);
  xor xor_3 (xor_1_out[2], in_3[2], SUB);
  xor xor_4 (xor_1_out[3], in_3[3], SUB);
  xor xor_5 (xor_1_out[4], in_3[4], SUB);
  xor xor_6 (xor_1_out[5], in_3[5], SUB);
  xor xor_7 (xor_1_out[6], in_3[6], SUB);
  xor xor_8 (xor_1_out[7], in_3[7], SUB);
  ADC adc_1 (.Ci(SUB), .in_2(A), .in_3(xor_1_out), .out_4(out_4), .Co(Co));

  // Notes on the sheet:
  //   B
  //   S
endmodule

module \logic  (
  input  [7:0] in_1,
  input  [7:0] in_2,
  input  [1:0] in_3,
  output [7:0] out_4
);

  wire [7:0] and_1_out, not_1_out, or_1_out, xor_1_out;

  assign and_1_out = in_1 & in_2;  // AND_Gate and_1, 8 bits wide
  assign not_1_out = ~in_1;  // NOT_Gate not_1, 8 bits wide
  assign or_1_out = in_1 | in_2;  // OR_Gate or_1, 8 bits wide
  assign xor_1_out = in_1 ^ in_2;  // XOR_Gate xor_1, 8 bits wide
  Multiplexer #(.select(2), .width(8)) multiplexer_1 (
    .in0(and_1_out), .in1(or_1_out), .in2(not_1_out), .in3(xor_1_out), .out(out_4), .sel(in_3));  // open: en
endmodule

module artic (
  input  [7:0] in_1,
  input  [7:0] in_2,
  input  [1:0] in_3,
  output out_4,
  output [7:0] out_5
);

  wire [7:0] divider_1_out, multiplier_1_out, substractor_1_out_4;

  substractor substractor_1 (.A(in_1), .in_3(in_2), .out_4(substractor_1_out_4), .SUB(in_3[0]), .Co(out_4));
  Multiplier multiplier_1 (.a(in_1), .b(in_2), .out(multiplier_1_out));  // open: cin, cout
  Divider divider_1 (.a(in_1), .b(in_2), .out(divider_1_out));  // open: upper, rem
  Multiplexer #(.select(2), .width(8)) multiplexer_1 (
    .in0(substractor_1_out_4), .in1(substractor_1_out_4), .in2(multiplier_1_out), .in3(divider_1_out),
    .out(out_5), .sel(in_3));  // open: en
endmodule

module move (
  input  [7:0] in_1,
  input  [2:0] in_2,
  input  [1:0] in_3,
  output [7:0] out_4
);

  wire [7:0] shifter_1_out, shifter_2_out, shifter_3_out, shifter_4_out;

  Shifter shifter_1 (.in(in_1), .\dist (in_2), .out(shifter_1_out));
  Shifter #(.shift("lr")) shifter_2 (.in(in_1), .\dist (in_2), .out(shifter_2_out));
  Shifter shifter_3 (.in(in_1), .\dist (in_2), .out(shifter_3_out));
  Shifter #(.shift("ar")) shifter_4 (.in(in_1), .\dist (in_2), .out(shifter_4_out));
  Multiplexer #(.select(2), .width(8)) multiplexer_1 (
    .in0(shifter_1_out), .in1(shifter_2_out), .in2(shifter_3_out), .in3(shifter_4_out), .out(out_4),
    .sel(in_3));  // open: en
endmodule

module Register (
  input  [7:0] in_1,
  input  [2:0] in_2,
  input  in_3,
  input  in_4,
  input  [2:0] in_5,
  input  [2:0] in_6,
  output [7:0] out_7,
  output [7:0] out_8
);

  wire and_1_out, and_2_out, and_3_out, and_4_out, and_5_out, and_6_out, and_7_out, and_8_out,
       decoder_1_out0, decoder_1_out1, decoder_1_out2, decoder_1_out3, decoder_1_out4, decoder_1_out5,
       decoder_1_out6, decoder_1_out7;
  wire [7:0] register_1_q, register_2_q, register_3_q, register_4_q, register_5_q, register_6_q,
       register_7_q, register_8_q;

  Decoder #(.select(3)) decoder_1 (
    .out0(decoder_1_out0), .out1(decoder_1_out1), .out2(decoder_1_out2), .out3(decoder_1_out3),
    .out4(decoder_1_out4), .out5(decoder_1_out5), .out6(decoder_1_out6), .out7(decoder_1_out7), .sel(in_2));  // open: en
  and and_1 (and_1_out, decoder_1_out0, in_3);
  and and_2 (and_2_out, decoder_1_out1, in_3);
  and and_3 (and_3_out, decoder_1_out2, in_3);
  and and_4 (and_4_out, decoder_1_out3, in_3);
  and and_5 (and_5_out, decoder_1_out4, in_3);
  and and_6 (and_6_out, decoder_1_out5, in_3);
  and and_7 (and_7_out, decoder_1_out6, in_3);
  and and_8 (and_8_out, decoder_1_out7, in_3);
  Register_part register_1 (.D(in_1), .en(and_1_out), .Q(register_1_q), .clk(in_4));  // open: clr
  Register_part register_2 (.D(in_1), .en(and_2_out), .Q(register_2_q), .clk(in_4));  // open: clr
  Register_part register_3 (.D(in_1), .en(and_3_out), .Q(register_3_q), .clk(in_4));  // open: clr
  Register_part register_4 (.D(in_1), .en(and_4_out), .Q(register_4_q), .clk(in_4));  // open: clr
  Register_part register_5 (.D(in_1), .en(and_5_out), .Q(register_5_q), .clk(in_4));  // open: clr
  Register_part register_6 (.D(in_1), .en(and_6_out), .Q(register_6_q), .clk(in_4));  // open: clr
  Register_part register_7 (.D(in_1), .en(and_7_out), .Q(register_7_q), .clk(in_4));  // open: clr
  Register_part register_8 (.D(in_1), .en(and_8_out), .Q(register_8_q), .clk(in_4));  // open: clr
  Multiplexer #(.select(3), .width(8)) multiplexer_1 (
    .in0(register_1_q), .in1(register_2_q), .in2(register_3_q), .in3(register_4_q), .in4(register_5_q),
    .in5(register_6_q), .in6(register_7_q), .in7(register_8_q), .out(out_7), .sel(in_5));  // open: en
  Multiplexer #(.select(3), .width(8)) multiplexer_2 (
    .in0(register_1_q), .in1(register_2_q), .in2(register_3_q), .in3(register_4_q), .in4(register_5_q),
    .in5(register_6_q), .in6(register_7_q), .in7(register_8_q), .out(out_8), .sel(in_6));  // open: en
endmodule

module danyuan (
  input  [7:0] in_1,
  input  in_2,
  input  in_3,
  input  in_4,
  output [7:0] out_5
);

  D_Flip_Flop d_ff_1 (.clk(in_4), .D(in_1[0]), .Q(out_5[0]), .en(in_2), .reset(in_3));  // open: Qn, preset
  D_Flip_Flop d_ff_2 (.clk(in_4), .D(in_1[1]), .Q(out_5[1]), .en(in_2), .reset(in_3));  // open: Qn, preset
  D_Flip_Flop d_ff_3 (.clk(in_4), .D(in_1[2]), .Q(out_5[2]), .en(in_2), .reset(in_3));  // open: Qn, preset
  D_Flip_Flop d_ff_4 (.clk(in_4), .D(in_1[3]), .Q(out_5[3]), .en(in_2), .reset(in_3));  // open: Qn, preset
  D_Flip_Flop d_ff_5 (.clk(in_4), .D(in_1[4]), .Q(out_5[4]), .en(in_2), .reset(in_3));  // open: Qn, preset
  D_Flip_Flop d_ff_6 (.clk(in_4), .D(in_1[5]), .Q(out_5[5]), .en(in_2), .reset(in_3));  // open: Qn, preset
  D_Flip_Flop d_ff_7 (.clk(in_4), .D(in_1[6]), .Q(out_5[6]), .en(in_2), .reset(in_3));  // open: Qn, preset
  D_Flip_Flop d_ff_8 (.clk(in_4), .D(in_1[7]), .Q(out_5[7]), .en(in_2), .reset(in_3));  // open: Qn, preset
endmodule

module Register2 (
  input  [7:0] in_1,
  input  [2:0] in_2,
  input  [2:0] in_3,
  input  [2:0] in_4,
  input  in_5,
  input  in_6,
  input  in_7,
  output [7:0] out_8,
  output [7:0] out_9
);

  wire and_1_out, and_2_out, and_3_out, and_4_out, and_5_out, and_6_out, and_7_out, and_8_out,
       decoder_1_out0, decoder_1_out1, decoder_1_out2, decoder_1_out3, decoder_1_out4, decoder_1_out5,
       decoder_1_out6, decoder_1_out7;
  wire [7:0] danyuan_1_out_5, danyuan_2_out_5, danyuan_3_out_5, danyuan_4_out_5, danyuan_5_out_5,
       danyuan_6_out_5, danyuan_7_out_5, danyuan_8_out_5;

  Decoder #(.select(3)) decoder_1 (
    .out0(decoder_1_out0), .out1(decoder_1_out1), .out2(decoder_1_out2), .out3(decoder_1_out3),
    .out4(decoder_1_out4), .out5(decoder_1_out5), .out6(decoder_1_out6), .out7(decoder_1_out7), .sel(in_2));  // open: en
  buf and_1 (and_1_out, decoder_1_out0);  // AND_Gate
  and and_2 (and_2_out, decoder_1_out1, in_6);
  and and_3 (and_3_out, decoder_1_out2, in_6);
  and and_4 (and_4_out, decoder_1_out3, in_6);
  and and_5 (and_5_out, decoder_1_out4, in_6);
  and and_6 (and_6_out, decoder_1_out5, in_6);
  and and_7 (and_7_out, decoder_1_out6, in_6);
  and and_8 (and_8_out, decoder_1_out7, in_6);
  danyuan danyuan_1 (.in_1(in_1), .in_2(and_1_out), .out_5(danyuan_1_out_5), .in_4(in_7), .in_3(in_5));
  danyuan danyuan_2 (.in_1(in_1), .in_2(and_2_out), .out_5(danyuan_2_out_5), .in_4(in_7), .in_3(in_5));
  danyuan danyuan_3 (.in_1(in_1), .in_2(and_3_out), .out_5(danyuan_3_out_5), .in_4(in_7), .in_3(in_5));
  danyuan danyuan_4 (.in_1(in_1), .in_2(and_4_out), .out_5(danyuan_4_out_5), .in_4(in_7), .in_3(in_5));
  danyuan danyuan_5 (.in_1(in_1), .in_2(and_5_out), .out_5(danyuan_5_out_5), .in_4(in_7), .in_3(in_5));
  danyuan danyuan_6 (.in_1(in_1), .in_2(and_6_out), .out_5(danyuan_6_out_5), .in_4(in_7), .in_3(in_5));
  danyuan danyuan_7 (.in_1(in_1), .in_2(and_7_out), .out_5(danyuan_7_out_5), .in_4(in_7), .in_3(in_5));
  danyuan danyuan_8 (.in_1(in_1), .in_2(and_8_out), .out_5(danyuan_8_out_5), .in_4(in_7), .in_3(in_5));
  Multiplexer #(.select(3), .width(8)) multiplexer_1 (
    .in0(danyuan_1_out_5), .in1(danyuan_2_out_5), .in2(danyuan_3_out_5), .in3(danyuan_4_out_5),
    .in4(danyuan_5_out_5), .in5(danyuan_6_out_5), .in6(danyuan_7_out_5), .in7(danyuan_8_out_5), .out(out_8),
    .sel(in_4));  // open: en
  Multiplexer #(.select(3), .width(8)) multiplexer_2 (
    .in0(danyuan_1_out_5), .in1(danyuan_2_out_5), .in2(danyuan_3_out_5), .in3(danyuan_4_out_5),
    .in4(danyuan_5_out_5), .in5(danyuan_6_out_5), .in6(danyuan_7_out_5), .in7(danyuan_8_out_5), .out(out_9),
    .sel(in_3));  // open: en
endmodule

module _16Register (
  input  [7:0] in_1,
  input  in_2,
  input  in_3,
  input  [3:0] in_4,
  input  [3:0] in_5,
  input  in_6,
  input  [3:0] in_7,
  output [7:0] out_8,
  output [7:0] out_9
);

  wire and_1_out, and_2_out, not_1_out;
  wire [7:0] register2_1_out_8, register2_1_out_9, register2_2_out_8, register2_2_out_9;

  not not_1 (not_1_out, in_7[3]);
  and and_1 (and_1_out, in_6, not_1_out);
  Register2 register2_1 (
    .in_1(in_1), .in_2(in_7[2:0]), .in_3(in_5[2:0]), .in_4(in_4[2:0]), .in_5(in_2), .in_6(and_1_out),
    .out_8(register2_1_out_8), .out_9(register2_1_out_9), .in_7(in_3));
  and and_2 (and_2_out, in_6, in_7[3]);
  Register2 register2_2 (
    .in_1(in_1), .in_2(in_7[2:0]), .in_3(in_5[2:0]), .in_4(in_4[2:0]), .in_5(in_2), .in_6(and_2_out),
    .out_8(register2_2_out_8), .out_9(register2_2_out_9), .in_7(in_3));
  Multiplexer #(.width(8)) multiplexer_1 (
    .in0(register2_1_out_9), .in1(register2_2_out_9), .out(out_9), .sel(in_5[3]));  // open: en
  Multiplexer #(.width(8)) multiplexer_2 (
    .in0(register2_1_out_8), .in1(register2_2_out_8), .out(out_8), .sel(in_4[3]));  // open: en
endmodule

module ID (
  input  [19:0] in_1,
  output [2:0] OP,
  output [3:0] RS,
  output [4:0] RT,
  output [4:0] out_5,
  output [3:0] RD,
  output [3:0] FUNCT,
  output [7:0] out_8,
  output [16:0] out_9
);


  assign FUNCT = in_1[3:0];
  assign OP = in_1[19:17];
  assign out_5 = in_1[12:8];
  assign out_8 = in_1[7:0];
  assign out_9 = in_1[16:0];
  assign RD = in_1[7:4];
  assign RS = in_1[16:13];
  assign RT = in_1[12:8];

  // Notes on the sheet:
  //   IMM1
  //   IMM2
endmodule

module CU (
  input  [2:0] in_1,
  output out_2,
  output out_3,
  output out_4,
  output out_5,
  output out_6,
  output out_7,
  output out_8
);

  wire not_1_out, not_2_out, not_3_out;

  not not_1 (not_1_out, in_1[2]);
  not not_2 (not_2_out, in_1[1]);
  not not_3 (not_3_out, in_1[0]);
  and R (out_2, not_1_out, not_2_out, not_3_out);
  and I (out_3, not_1_out, not_2_out, in_1[0]);
  and LOAD (out_4, not_1_out, in_1[1], not_3_out);
  and STORE (out_5, not_1_out, in_1[1], in_1[0]);
  and BEQ (out_6, in_1[2], not_2_out, not_3_out);
  and BNE (out_7, in_1[2], not_2_out, in_1[0]);
  and J (out_8, in_1[2], in_1[1], in_1[0]);
endmodule

module PC (
  input  in_1,
  input  [16:0] in_2,
  input  in_3,
  input  in_4,
  input  [7:0] in_5,
  input  in_6,
  input  in_7,
  output [16:0] out_8
);

  wire [16:0] adder_1_out, adder_2_out, bit_extender_1_out, multiplexer_1_out, multiplexer_2_out;

  Multiplexer #(.width(17)) multiplexer_1 (
    .in0(17'h1), .in1(adder_2_out), .out(multiplexer_1_out), .sel(in_1));  // open: en
  assign bit_extender_1_out = {{9{1'b0}}, in_5};  // Bit_Extender bit_extender_1
  Adder #(.width(17)) adder_1 (.a(out_8), .b(multiplexer_1_out), .out(adder_1_out));  // open: cin, cout
  Adder #(.width(17)) adder_2 (.a(bit_extender_1_out), .b(17'h1), .out(adder_2_out));  // open: cin, cout
  Multiplexer #(.width(17)) multiplexer_2 (
    .in0(adder_1_out), .in1(in_2), .out(multiplexer_2_out), .sel(in_4));  // open: en
  Register_part #(.width(17)) register_1 (.D(multiplexer_2_out), .en(in_3), .Q(out_8), .clk(in_6), .clr(in_7));
endmodule

module FUNCT (
  input  [3:0] in_1,
  output out_2,
  output out_3,
  output out_4,
  output out_5,
  output out_6,
  output out_7,
  output out_8,
  output out_9,
  output out_10,
  output out_11,
  output out_12,
  output out_13
);

  wire not_1_out, not_2_out, not_3_out, not_4_out;

  not not_1 (not_1_out, in_1[1]);
  not not_2 (not_2_out, in_1[0]);
  not not_3 (not_3_out, in_1[2]);
  not not_4 (not_4_out, in_1[3]);
  and ADD_ADDI (out_2, not_4_out, not_3_out, not_1_out, not_2_out);
  and SUB_SUBI (out_3, not_4_out, not_3_out, not_1_out, in_1[0]);
  and MUL_MULI (out_4, not_4_out, not_3_out, in_1[1], not_2_out);
  and DIV_DIVI (out_5, not_4_out, not_3_out, in_1[1], in_1[0]);
  and AND (out_6, not_4_out, in_1[2], not_1_out, not_2_out);
  and OR (out_7, not_4_out, in_1[2], not_1_out, in_1[0]);
  and NOT_5 (out_8, not_4_out, in_1[1], in_1[2], not_2_out);
  and XOR (out_9, not_4_out, in_1[1], in_1[2], in_1[0]);
  and SLL (out_10, in_1[3], not_3_out, not_1_out, not_2_out);
  and SLR (out_11, in_1[3], not_3_out, not_1_out, in_1[0]);
  and SAL (out_12, in_1[3], not_3_out, in_1[2], not_2_out);
  and SAR (out_13, in_1[0], not_3_out, in_1[2], in_1[0]);
endmodule

module CU_all (
  input  [2:0] in_1,
  input  [3:0] in_2,
  output regdst,
  output memtoreg,
  output regwrite,
  output memwrite,
  output BRANCHBEQ,
  output BRANCHBNE,
  output JUMP,
  output immchoose1,
  output immchoose2,
  output [3:0] out_12
);

  wire cu_1_out_2, cu_1_out_4;

  CU cu_1 (
    .out_2(cu_1_out_2), .out_3(immchoose1), .in_1(in_1), .out_4(cu_1_out_4), .out_5(memwrite),
    .out_6(BRANCHBEQ), .out_7(BRANCHBNE), .out_8(JUMP));
  or or_1 (regdst, cu_1_out_2, immchoose1);
  or or_2 (regwrite, cu_1_out_2, immchoose1, cu_1_out_4);
  or or_3 (immchoose2, cu_1_out_4, memwrite);
  Multiplexer #(.select(2), .width(4)) multiplexer_1 (
    .in0(in_2), .in1(4'b0000), .in2(4'b0001), .out(out_12), .sel(in_1[2:1]));  // open: in3, en
  or or_4 (memtoreg, cu_1_out_2, immchoose1);
endmodule
